// Logisim project processor_riscv_evolution.circ as structural Verilog
module ALU (
  input  [2:0] F,
  input  [31:0] A,
  input  [31:0] B,
  output Zero,
  output [31:0] Y
);

  wire bitselector_1_out, comparator_1_lt;
  wire [31:0] adder_1_out, and_1_out, bit_extender_1_out, bit_extender_2_out, multiplier_1_out, or_1_out,
       xor_1_out;

  BitSelector #(.width(3)) bitselector_1 (.in(F), .out(bitselector_1_out), .sel(2'b00));
  assign bit_extender_1_out = {{31{bitselector_1_out}}, bitselector_1_out};  // Bit_Extender bit_extender_1
  assign xor_1_out = bit_extender_1_out ^ B;  // XOR_Gate xor_1, 32 bits wide
  Multiplexer #(.disabled("Z"), .select(3), .width(32)) multiplexer_1 (
    .in0(adder_1_out), .in1(adder_1_out), .in2(and_1_out), .in3(or_1_out), .in4(multiplier_1_out),
    .in5(bit_extender_2_out), .out(Y), .sel(F));  // open: in6, in7
  Adder #(.width(32)) adder_1 (.a(A), .b(xor_1_out), .out(adder_1_out), .cin(bitselector_1_out));  // open: cout
  Multiplier #(.width(32)) multiplier_1 (.a(A), .b(B), .out(multiplier_1_out));  // open: cin, cout
  assign and_1_out = A & B;  // AND_Gate and_1, 32 bits wide
  assign or_1_out = A | B;  // OR_Gate or_1, 32 bits wide
  assign bit_extender_2_out = {{31{1'b0}}, comparator_1_lt};  // Bit_Extender bit_extender_2
  Comparator #(.mode("unsigned"), .width(32)) comparator_1 (.a(A), .b(B), .lt(comparator_1_lt));  // open: gt, eq
  Comparator #(.mode("unsigned"), .width(32)) comparator_2 (.a({32{1'b0}}), .b(Y), .eq(Zero));  // open: gt, lt
endmodule

module Datapath (
  output [31:0] t2
);

  wire alu_1_zero, and_1_out, clock_1_out, CU_alusrc, CU_branch, CU_regwrite;
  wire [2:0] CU_alucontrol, rom_1_data_2, rom_1_data_4, rom_1_data_5;
  wire [4:3] rom_1_data_6;
  wire [7:0] adder_1_out, adder_2_out, multiplexer_1_out, register_1_q, shifter_1_out;
  wire [12:3] rom_1_data_3;
  wire [19:0] rom_1_data;
  wire [31:0] alu_1_y, bit_extender_1_out, bit_extender_2_out, bit_extender_3_out, multiplexer_2_out, RF_rd1,
       RF_rd2;
  wire [31:8] adder_1_out_2, adder_2_out_2;

  // Probe on adder_2_out
  Multiplexer #(.width(8)) multiplexer_1 (
    .in0(adder_1_out), .in1(adder_2_out), .out(multiplexer_1_out), .sel(and_1_out));
  and and_1 (and_1_out, CU_branch, alu_1_zero);
  Register register_1 (.D(multiplexer_1_out), .en(1'b1), .clk(clock_1_out), .Q(register_1_q));  // open: clr
  assign bit_extender_1_out = {{24{register_1_q[7]}}, register_1_q};  // Bit_Extender bit_extender_1
  // Probe on bit_extender_1_out
  Adder #(.width(32)) adder_1 (
    .a(bit_extender_1_out), .b(32'h4), .out({adder_1_out_2, adder_1_out}));  // open: cin, cout
  Shifter #(.shift("lr")) shifter_1 (.in(register_1_q), .\dist (3'b010), .out(shifter_1_out));
  Adder #(.width(32)) adder_2 (
    .a(bit_extender_1_out), .b(bit_extender_2_out), .out({adder_2_out_2, adder_2_out}));  // open: cin, cout
  // Probe on bit_extender_2_out
  assign bit_extender_2_out = {{19{rom_1_data_3[12]}}, {rom_1_data_3[12], rom_1_data_2[0], rom_1_data_3[10:3], rom_1_data_2[2:1], 1'b0}};  // Bit_Extender bit_extender_2
  // Probe on shifter_1_out
  ROM #(.dataWidth(32)) rom_1 (
    .addr(shifter_1_out),
    .data({rom_1_data_3[12], rom_1_data_3[10:5], rom_1_data_6, rom_1_data_5, rom_1_data[19:18], rom_1_data_4, rom_1_data[14:12], rom_1_data_3[4:3], rom_1_data_2, rom_1_data[6:0]}));
  Clock clock_1 (.out(clock_1_out));
  // Probe on {rom_1_data_3[12], rom_1_data_3[10:5], rom_1_data_6, rom_1_data_5, rom_1_data[19:18], rom_1_data_4, rom_1_data[14:12], rom_1_data_3[4:3], rom_1_data_2, rom_1_data[6:0]}
  assign bit_extender_3_out = {{20{rom_1_data_3[12]}}, {rom_1_data_3[12], rom_1_data_3[10:5], rom_1_data_6, rom_1_data_5}};  // Bit_Extender bit_extender_3
  ControlUnit CU (
    .Instruction({rom_1_data_3[12], rom_1_data_3[10:5], rom_1_data_6, rom_1_data_5, rom_1_data[19:18], rom_1_data_4, rom_1_data[14:12], rom_1_data_3[4:3], rom_1_data_2, rom_1_data[6:0]}),
    .RegWrite(CU_regwrite), .ALUSrc(CU_alusrc), .Branch(CU_branch), .ALUControl(CU_alucontrol));
  RegisterFile RF (
    .WD3(alu_1_y), .CLK(clock_1_out), .A2(rom_1_data_5), .A1(rom_1_data_4), .A3(rom_1_data_2),
    .WE3(CU_regwrite), .RD1(RF_rd1), .RD2(RF_rd2), .T2(t2));
  Multiplexer #(.disabled("Z"), .width(32)) multiplexer_2 (
    .in0(RF_rd2), .in1(bit_extender_3_out), .out(multiplexer_2_out), .sel(CU_alusrc));
  // Probe on CU_alucontrol
  ALU alu_1 (.A(RF_rd1), .B(multiplexer_2_out), .F(CU_alucontrol), .Y(alu_1_y), .Zero(alu_1_zero));
  // Probe on alu_1_y

  // Notes on the sheet:
  //   Zero
  //   Branch
  //   contents of rom_1 (hex, n*v repeats v):
  //   300293 100313 100393 128213 430863 26383b3 130313 fe000ae3 63
  //   B-type
endmodule

module RegisterFile (
  input  CLK,
  input  [2:0] A1,
  input  [31:0] WD3,
  input  [2:0] A2,
  input  WE3,
  input  [2:0] A3,
  output [31:0] RD1,
  output [31:0] RD2,
  output [31:0] T2
);

  wire and_1_out, and_2_out, and_3_out, and_4_out, and_5_out, and_6_out, and_7_out, decoder_1_out0,
       decoder_1_out1, decoder_1_out2, decoder_1_out3, decoder_1_out4, decoder_1_out5, decoder_1_out6,
       decoder_1_out7;
  wire [31:0] register_1_q, register_2_q, register_3_q, register_4_q, register_5_q, register_6_q;

  Decoder #(.select(3)) decoder_1 (
    .out0(decoder_1_out0), .out1(decoder_1_out1), .out2(decoder_1_out2), .out3(decoder_1_out3),
    .out4(decoder_1_out4), .out5(decoder_1_out5), .out6(decoder_1_out6), .out7(decoder_1_out7), .sel(A3));  // open: en
  and and_1 (and_1_out, WE3, decoder_1_out1);
  and and_2 (and_2_out, WE3, decoder_1_out2);
  and and_3 (and_3_out, WE3, decoder_1_out3);
  and and_4 (and_4_out, WE3, decoder_1_out4);
  and and_5 (and_5_out, WE3, decoder_1_out5);
  and and_6 (and_6_out, WE3, decoder_1_out6);
  and and_7 (and_7_out, WE3, decoder_1_out7);
  Register #(.width(32)) register_1 (.D(WD3), .en(and_1_out), .clk(CLK), .Q(register_1_q));  // open: clr
  Register #(.width(32)) register_2 (.D(WD3), .en(and_2_out), .clk(CLK), .Q(register_2_q));  // open: clr
  Register #(.width(32)) register_3 (.D(WD3), .en(and_3_out), .clk(CLK), .Q(register_3_q));  // open: clr
  Register #(.width(32)) register_4 (.D(WD3), .en(and_4_out), .clk(CLK), .Q(register_4_q));  // open: clr
  Register #(.width(32)) register_5 (.D(WD3), .en(and_5_out), .clk(CLK), .Q(register_5_q));  // open: clr
  Register #(.width(32)) register_6 (.D(WD3), .en(and_6_out), .clk(CLK), .Q(register_6_q));  // open: clr
  Register #(.width(32)) register_7 (.D(WD3), .en(and_7_out), .clk(CLK), .Q(T2));  // open: clr
  Multiplexer #(.enable("true"), .select(3), .width(32)) multiplexer_1 (
    .in0({32{1'b0}}), .in1(register_1_q), .in2(register_2_q), .in3(register_3_q), .in4(register_4_q),
    .in5(register_5_q), .in6(register_6_q), .in7(T2), .out(RD1), .sel(A1));  // open: en
  Multiplexer #(.enable("true"), .select(3), .width(32)) multiplexer_2 (
    .in0({32{1'b0}}), .in1(register_1_q), .in2(register_2_q), .in3(register_3_q), .in4(register_4_q),
    .in5(register_5_q), .in6(register_6_q), .in7(T2), .out(RD2), .sel(A2));  // open: en
endmodule

module ControlUnit (
  input  [31:0] Instruction,
  output RegWrite,
  output ALUSrc,
  output [2:0] ALUControl,
  output Branch
);

  wire and_1_out, comparator_3_eq;
  wire [2:0] multiplexer_1_out;

  and and_1 (and_1_out, Instruction[25], comparator_3_eq);
  Comparator #(.mode("unsigned"), .width(7)) comparator_1 (
    .a(Instruction[6:0]), .b(7'b1100011), .eq(Branch));  // open: gt, lt
  Comparator #(.mode("unsigned"), .width(7)) comparator_2 (
    .a(Instruction[6:0]), .b(7'b0010011), .eq(ALUSrc));  // open: gt, lt
  Comparator #(.mode("unsigned"), .width(7)) comparator_3 (
    .a(Instruction[6:0]), .b(7'b0110011), .eq(comparator_3_eq));  // open: gt, lt
  Multiplexer #(.width(3)) multiplexer_1 (.in0(3'b000), .in1(3'b001), .out(multiplexer_1_out), .sel(Branch));
  or or_1 (RegWrite, ALUSrc, comparator_3_eq);
  Multiplexer #(.width(3)) multiplexer_2 (.in0(multiplexer_1_out), .in1(3'b100), .out(ALUControl), .sel(and_1_out));
endmodule

module Tests (
  output [31:0] Y,
  output [3:0] out_2,
  output [7:0] out_3
);


  assign out_2 = 4'b0010;
  assign out_3 = 8'h22;
  assign Y = 32'hf4010207;

  // Notes on the sheet:
  //   binary values in Logisim. Convince yourself how the bits are displayed.
  //   Example 1: A simple example that illustrates how 32-bit values are displayed as 
  //   Example 2) An example of how to extra certain bits from a (in this case) 32-bit wire. Here we extract the bits 8..11 from the 32-bit wire.
  //   Example 3) Sometimes it is useful to extra bits from different position and the re-assemble them. In this case, we extract bits 8..11 and bits 15..18 and assemble them into an 8-bit wire.
endmodule
